# Fritzing sketch chickenman (saved by Fritzing 0.9.4)
breadboards: 3

parts:
  U1 = NodeMCU V3.0
  R1 = Resistor [tolerance=±5% resistance=330 package=THT]
  LED1 = LED - 5mm [color="Red (633nm)" package="5 mm [THT]"]
  LED2 = LED - 5mm [color="Green (555nm)" package="5 mm [THT]"]
  LED3 = LED - 5mm [color="Blue (430nm)" package="5 mm [THT]"]
  U2 = NodeMCU V3.0
  R2 = Resistor [tolerance=±5% resistance=330 package=THT]
  LED4 = LED - 5mm [color="Red (633nm)" package="5 mm [THT]"]
  LED5 = LED - 5mm [color="Green (555nm)" package="5 mm [THT]"]
  LED6 = LED - 5mm [color="Blue (430nm)" package="5 mm [THT]"]
  U3 = NodeMCU V3.0
  LED7 = LED - 5mm [color="Red (633nm)" package="5 mm [THT]"]
  LED8 = LED - 5mm [color="Green (555nm)" package="5 mm [THT]"]
  LED9 = LED - 5mm [color="Blue (430nm)" package="5 mm [THT]"]
  R3 = Resistor [tolerance=±5% resistance=330 package=THT]
  R4 = Resistor [tolerance=±5% resistance=330 package=THT]

nets:
  N1: U1.D1, LED1.anode
  N2: U1.D2, LED2.anode
  N3: U1.D3, LED3.anode
  N4: U1.GND#6, U1.D7, U1.GND#13, U1.GND#16, U1.GND#33, R1.Pin_0
  N5: R1.Pin_1, LED1.cathode, LED2.cathode, LED3.cathode
  N6: U2.D1, LED4.anode
  N7: U2.D2, LED5.anode
  N8: U2.D3, LED6.anode
  N9: U2.GND#6, U2.D7, U2.GND#13, U2.GND#16, U2.GND#33, R2.Pin_0, R4.Pin_0
  N10: R2.Pin_1, LED6.cathode
  N11: LED4.cathode, R4.Pin_1
  N12: LED5.cathode, R3.Pin_1
  N13: U3.D1, LED7.anode
  N14: U3.D2, LED8.anode
  N15: U3.D3, LED9.anode
  N16: U3.3V3, LED7.cathode, LED8.cathode, LED9.cathode
  N17: U3.GND#6, U3.D7, U3.GND#13, U3.GND#16, U3.GND#33

notes:
  Model A:
  Will burn out LEDs
  Model B:
  LEDs will last longer
  Model C:
  LEDs will last the longest

custom parts:
  NodeMCU V3.0: ESP8266 based NodeMCU
